# Fritzing sketch esquema (saved by Fritzing 0.9.3b)
breadboards: 1

parts:
  R1 = Resistor [tolerance=±5% resistance=10k package=THT]
  R2 = Resistor [tolerance=±5% resistance=10k package=THT]
  R3 = Resistor [tolerance=±5% resistance=10k package=THT]
  R4 = Resistor [tolerance=±5% resistance=10k package=THT]
  R5 = Photocell (LDR) [package=THT]
  R6 = Photocell (LDR) [package=THT]
  R7 = Photocell (LDR) [package=THT]
  R8 = Photocell (LDR) [package=THT]
  J1 = Basic Servo
  J2 = Basic Servo
  Componente1 = Arduino Uno (Rev3)

nets:
  N1: R1.Pin_0, R5.pin_1, Componente1.A1
  GND: R1.Pin_1, R2.Pin_1, R3.Pin_1, R4.Pin_1, J1.gnd, J2.gnd, Componente1.GND
  N2: R2.Pin_0, R7.pin_1, Componente1.A3
  N3: R3.Pin_0, R6.pin_1, Componente1.A2
  N4: R4.Pin_0, R8.pin_1, Componente1.A0
  VCC: R5.pin_0, R6.pin_0, R7.pin_0, R8.pin_0, J2.vcc, Componente1.5V
  N5: J1.pulse, Componente1.D9_PWM
  N6: J2.pulse, Componente1.D10_PWM/SS

notes:
  HORIZONTAL
  PIN DW 9
  VERTICAL
  PIN DW 10
  SUPERIOR
  ESQUERDO
  PIN A0
  IFERIOR
  ESQUERDO
  PIN A2
  INFERIOR
  DIREITO
  PIN A3
  SUPERIOR
  DIREITO
  PIN A1
  SENSOR LDR
